# Fritzing sketch Pot to Servo Control 6 (saved by Fritzing 0.9.2b)
breadboards: 1

parts:
  R1 = Rotary Potentiometer (Small) [maximum_resistance=100kΩ package=THT]
  J2 = Basic Servo
  Part2 = Arduino Mega 2560 (Rev3)

nets:
  VCC: R1.leg1, J2.vcc, Part2.5V
  N1: R1.wiper, Part2.A0
  N2: R1.leg2, J2.gnd
  N3: J2.pulse, Part2.D3_PWM
